// Digital circuit lab2_part2.dig as structural Verilog
module lab2_part2 (
  input  in0,
  input  in1,
  input  in2,
  input  in3,
  output seg_a,
  output seg_f,
  output seg_b,
  output seg_g,
  output seg_e,
  output seg_c,
  output seg_d,
  output seg_dp,
  output sign_a,
  output sign_f,
  output sign_b,
  output sign_g,
  output sign_e,
  output sign_c,
  output sign_d,
  output sign_dp
);

  wire and_1_out, and_2_out, and_3_out, and_4_out, and_5_out, and_6_out, and_7_out, and_8_out, and_9_out,
       and_10_out, and_11_out, and_12_out, and_13_out, and_14_out, and_15_out, and_16_out, and_17_out,
       and_18_out, and_19_out, and_20_out, and_21_out, and_22_out, and_23_out, and_24_out, and_25_out,
       and_26_out, and_27_out, and_28_out, and_29_out, and_30_out, and_31_out, and_32_out, and_33_out,
       and_34_out, and_35_out;

  Seven_Seg seven_seg_1 (.a(1'b0), .b(1'b0), .c(1'b0), .d(1'b0), .e(1'b0), .f(1'b0), .g(in3), .dp(1'b0));
  Seven_Seg seven_seg_2 (.a(seg_a), .b(seg_b), .c(seg_c), .d(seg_d), .e(seg_e), .f(seg_f), .g(seg_g), .dp(1'b0));
  and and_1 (and_1_out, ~in0, ~in1, in2, ~in3);  // And
  and and_2 (and_2_out, in0, in1, in2, in3);
  and and_3 (and_3_out, in0, ~in1, ~in2, ~in3);  // And
  and and_4 (and_4_out, in0, ~in1, ~in2, ~in3);  // And
  nor nor_1 (seg_d, and_1_out, and_4_out, and_2_out, and_6_out, and_8_out, and_9_out);
  and and_5 (and_5_out, ~in0, ~in1, in2, ~in3);  // And
  and and_6 (and_6_out, ~in0, ~in1, in2, in3);  // And
  and and_7 (and_7_out, in0, in1, in2, in3);
  nor nor_2 (seg_a, and_10_out, and_7_out, and_5_out, and_3_out);
  and and_8 (and_8_out, in0, ~in1, ~in2, in3);  // And
  and and_9 (and_9_out, in0, in1, in2, ~in3);  // And
  and and_10 (and_10_out, ~in0, ~in1, in2, in3);  // And
  and and_11 (and_11_out, in0, ~in1, in2, ~in3);  // And
  and and_12 (and_12_out, ~in0, in1, ~in2, in3);  // And
  and and_13 (and_13_out, ~in0, in1, in2, ~in3);  // And
  nor nor_3 (seg_b, and_18_out, and_15_out, and_13_out, and_11_out);
  or or_1 (seg_e, and_12_out, and_16_out, and_14_out, and_17_out, and_19_out, and_21_out);
  and and_14 (and_14_out, ~in0, ~in1, ~in2, ~in3);  // And
  and and_15 (and_15_out, in0, in1, ~in2, in3);  // And
  and and_16 (and_16_out, ~in0, in1, in2, in3);  // And
  and and_17 (and_17_out, ~in0, in1, ~in2, ~in3);  // And
  and and_18 (and_18_out, ~in0, in1, ~in2, in3);  // And
  and and_19 (and_19_out, ~in0, in1, in2, ~in3);  // And
  and and_20 (and_20_out, ~in0, in1, ~in2, ~in3);  // And
  and and_21 (and_21_out, ~in0, ~in1, ~in2, in3);  // And
  nor nor_4 (seg_c, and_22_out, and_20_out);
  and and_22 (and_22_out, ~in0, in1, in2, in3);  // And
  and and_23 (and_23_out, ~in0, in1, in2, ~in3);  // And
  and and_24 (and_24_out, ~in0, ~in1, ~in2, ~in3);  // And
  and and_25 (and_25_out, in0, ~in1, ~in2, in3);  // And
  or or_2 (seg_f, and_24_out, and_23_out, and_30_out, and_26_out, and_32_out, and_33_out, and_35_out, and_34_out);
  and and_26 (and_26_out, ~in0, ~in1, in2, ~in3);  // And
  and and_27 (and_27_out, in0, in1, in2, in3);
  and and_28 (and_28_out, in0, in1, in2, ~in3);  // And
  nor nor_5 (seg_g, and_29_out, and_31_out, and_27_out, and_28_out, and_25_out);
  and and_29 (and_29_out, in0, ~in1, ~in2, ~in3);  // And
  and and_30 (and_30_out, ~in0, in1, ~in2, in3);  // And
  and and_31 (and_31_out, ~in0, ~in1, ~in2, ~in3);  // And
  and and_32 (and_32_out, in0, in1, ~in2, in3);  // And
  and and_33 (and_33_out, in0, ~in1, in2, ~in3);  // And
  and and_34 (and_34_out, ~in0, ~in1, in2, in3);  // And
  and and_35 (and_35_out, ~in0, ~in1, ~in2, in3);  // And

  assign seg_dp = 1'b0;
  assign sign_a = 1'b0;
  assign sign_b = 1'b0;
  assign sign_c = 1'b0;
  assign sign_d = 1'b0;
  assign sign_dp = 1'b0;
  assign sign_e = 1'b0;
  assign sign_f = 1'b0;
  assign sign_g = in3;

  // Notes on the sheet:
  //   Interface (do not edit the content inside this box)
  //   Outputs:
  //   Inputs
  //   Sign
  //   Decimal Number
endmodule

/* Test case:
in3 in2 in1 in0  sign_a sign_b sign_c sign_d sign_e sign_f sign_g  seg_a seg_b seg_c seg_d seg_e seg_f seg_g
 0   0   0   0    0      0      0      0      0      0      0       1     1     1     1     1     1     0
*/
